// Logisim project 4bitadder.circ as structural Verilog: 1 circuit, main circuit main
module main (
  input  Ao,
  input  Bo,
  input  A1,
  input  B1,
  input  A2,
  input  B2,
  input  A3,
  input  B3
);

  wire and_1_out, and_2_out, and_3_out, and_4_out, and_5_out, and_6_out, and_7_out, or_1_out, or_2_out,
       or_3_out, xor_1_out, xor_2_out, xor_3_out, xor_4_out, xor_5_out, xor_6_out, xor_7_out;

  xor xor_1 (xor_1_out, Ao, Bo);
  xor xor_2 (xor_2_out, A1, B1);
  xor xor_3 (xor_3_out, A2, B2);
  xor xor_4 (xor_4_out, A3, B3);
  and and_1 (and_1_out, Ao, Bo);
  and and_2 (and_2_out, A1, B1);
  and and_3 (and_3_out, and_1_out, xor_2_out);
  xor xor_5 (xor_5_out, xor_3_out, or_1_out);
  and and_4 (and_4_out, or_1_out, xor_3_out);
  and and_5 (and_5_out, B2, A2);
  and and_6 (and_6_out, or_2_out, xor_4_out);
  and and_7 (and_7_out, B3, A3);
  xor xor_6 (xor_6_out, xor_2_out, and_1_out);
  xor xor_7 (xor_7_out, xor_4_out, or_2_out);
  or or_1 (or_1_out, and_2_out, and_3_out);
  or or_2 (or_2_out, and_4_out, and_5_out);
  or or_3 (or_3_out, and_6_out, and_7_out);
  LED led_1 (.in(xor_1_out));
  LED led_2 (.in(xor_6_out));
  LED led_3 (.in(xor_5_out));
  LED led_4 (.in(xor_7_out));
  LED led_5 (.in(or_3_out));

  // Notes on the sheet:
  //   S1
  //   S2
  //   So
  //   S3
  //   Co
endmodule
