// Logisim project D_to_JK.circ as structural Verilog: 1 circuit, main circuit main
module main (
  input  J,
  input  in_2,
  output Qnext
);

  wire clock_1_out, nand_1_out, nand_2_out, nand_3_out, nand_4_out, nand_5_out, nand_6_out, nand_7_out,
       nand_8_out;

  nand nand_1 (nand_1_out, in_2, in_2);
  nand nand_2 (nand_2_out, Qnext, J);
  nand nand_3 (nand_3_out, nand_1_out, nand_8_out);
  nand nand_4 (nand_4_out, nand_2_out, nand_3_out);
  nand nand_5 (nand_5_out, nand_4_out, nand_4_out);
  Clock clock_1 (.out(clock_1_out));
  nand nand_6 (nand_6_out, nand_4_out, clock_1_out);
  nand nand_7 (nand_7_out, clock_1_out, nand_5_out);
  nand nand_8 (nand_8_out, nand_6_out, Qnext);
  nand nand_9 (Qnext, nand_8_out, nand_7_out);
  LED Qn (.in(nand_8_out));

  // Notes on the sheet:
  //   D
  //   !!!
endmodule
