// Logisim project JK_to_D.circ as structural Verilog: 1 circuit, main circuit main
module main (
  input  D,
  output Qnext
);

  wire CLK_out, nand_1_out, nand_2_out, nand_3_out, nand_4_out;

  nand nand_1 (nand_1_out, D, D);
  Clock CLK (.out(CLK_out));
  nand nand_2 (nand_2_out, Qnext, D, CLK_out);
  nand nand_3 (nand_3_out, CLK_out, nand_1_out, nand_4_out);
  nand nand_4 (nand_4_out, nand_2_out, Qnext);
  nand nand_5 (Qnext, nand_4_out, nand_3_out);
  LED Q (.in(nand_4_out));

  // Notes on the sheet:
  //   J
  //   k
  //   !!!
endmodule
