// Logisim project SR_to_JK.circ as structural Verilog: 1 circuit, main circuit main
module main (
  input  J,
  input  in_2,
  output Qnext
);

  wire clock_1_out, nand_1_out, nand_2_out, nand_3_out, nand_4_out, nand_5_out, nand_6_out, nand_7_out;

  nand nand_1 (nand_1_out, Qnext, J);
  nand nand_2 (nand_2_out, in_2, nand_7_out);
  nand nand_3 (nand_3_out, nand_1_out, nand_1_out);
  Clock clock_1 (.out(clock_1_out));
  nand nand_4 (nand_4_out, nand_2_out, nand_2_out);
  nand nand_5 (nand_5_out, nand_3_out, clock_1_out);
  nand nand_6 (nand_6_out, clock_1_out, nand_4_out);
  nand nand_7 (nand_7_out, nand_5_out, Qnext);
  nand nand_8 (Qnext, nand_7_out, nand_6_out);
  LED Qn (.in(nand_7_out));

  // Notes on the sheet:
  //   K
  //   S
  //   R
  //   !!!
endmodule
