// Logisim project binary_to_grey.circ as structural Verilog: 1 circuit, main circuit main
module main (
  input  B3,
  input  B2,
  input  B1,
  input  B0
);

  wire xor_1_out, xor_2_out, xor_3_out;

  xor xor_1 (xor_1_out, B3, B2);
  xor xor_2 (xor_2_out, B2, B1);
  xor xor_3 (xor_3_out, B1, B0);
  LED G3 (.in(B3));
  LED led_1 (.in(xor_1_out));
  LED led_2 (.in(xor_2_out));
  LED led_3 (.in(xor_3_out));

  // Notes on the sheet:
  //   G2
  //   G1
  //   G0
endmodule
